// Logisim project bus-control-logic.circ as structural Verilog: 1 circuit, main circuit main
module main (
  output BC0,
  output BC1,
  output out_3,
  output BUSCTL0,
  output BUSCTL_1,
  output out_6,
  output out_7
);

  wire and_1_out, and_2_out, and_3_out, and_4_out, and_8_out, and_9_out, and_10_out, and_11_out,
       button_1_out, not_1_out, not_2_out, not_3_out, not_4_out, not_5_out, not_6_out, not_7_out, not_8_out,
       not_9_out, not_10_out, not_11_out, random_3_out, random_4_out, random_5_out, TCSI_ISP_MISO_out;
  wire [2:0] DCS_ISP_OUT_out, ISP_SCLK_out, RCS_ISP_OUT_out, TCS_ISP_OUT_out;
  wire [3:2] counter_1_q;

  Clock ISP_SCLK (.out(ISP_SCLK_out[0]));
  Button button_1 (.out(button_1_out));
  not not_1 (not_1_out, BC0);
  not not_2 (not_2_out, BC1);
  not not_3 (not_3_out, BC1);
  not not_4 (not_4_out, BC0);
  and and_1 (and_1_out, BC0, BC1);
  and and_2 (and_2_out, not_1_out, not_2_out);
  Random #(.width(1), .seed(1)) random_1 (.clk(ISP_SCLK_out[0]), .next(1'b1), .out(ISP_SCLK_out[1]));  // open: clr
  Random #(.width(1), .seed(1), .trigger("falling")) random_2 (
    .clk(ISP_SCLK_out[0]), .next(1'b1), .out(ISP_SCLK_out[2]));  // open: clr
  Counter #(.width(4), .max('hf)) counter_1 (
    .count(1'b1), .Q({counter_1_q, BC1, BC0}), .clk(button_1_out), .clr(counter_1_q[2]));  // open: load, D, carry
  and and_3 (and_3_out, BC0, not_3_out);
  and and_4 (and_4_out, not_4_out, BC1);
  LED ISP_SCLK_2 (.in(ISP_SCLK_out[0]));
  LED ISP_MOSI (.in(ISP_SCLK_out[1]));
  LED ISP_RST (.in(ISP_SCLK_out[2]));
  LED ISP_MISO (.in(TCSI_ISP_MISO_out));
  not not_5 (not_5_out, and_2_out);
  not not_6 (not_6_out, and_2_out);
  not not_7 (not_7_out, and_2_out);
  and and_5 (out_3, and_3_out, not_5_out);
  and and_6 (out_6, and_4_out, not_6_out);
  and and_7 (out_7, and_1_out, not_7_out);
  assign TCSI_ISP_MISO_out = out_7 ? random_5_out : 1'bz;  // Controlled_Buffer TCSI_ISP_MISO
  not not_8 (not_8_out, BC1);
  not not_9 (not_9_out, BC0);
  not not_10 (not_10_out, BC0);
  not not_11 (not_11_out, BC1);
  assign RCS_ISP_OUT_out = out_3 ? ISP_SCLK_out : 3'bz;  // Controlled_Buffer RCS_ISP_OUT
  assign TCSI_ISP_MISO_out = out_3 ? random_3_out : 1'bz;  // Controlled_Buffer TCSI_ISP_MISO_2
  assign DCS_ISP_OUT_out = out_6 ? ISP_SCLK_out : 3'bz;  // Controlled_Buffer DCS_ISP_OUT
  assign TCSI_ISP_MISO_out = out_6 ? random_4_out : 1'bz;  // Controlled_Buffer TCSI_ISP_MISO_3
  assign TCS_ISP_OUT_out = out_7 ? ISP_SCLK_out : 3'bz;  // Controlled_Buffer TCS_ISP_OUT
  and and_8 (and_8_out, BC0, not_8_out);
  and and_9 (and_9_out, not_9_out, BC1);
  LED RCS_PGM (.in(and_8_out));
  and and_10 (and_10_out, BC0, BC1);
  LED DCS_PGM (.in(and_9_out));
  LED TCS_PGM (.in(and_10_out));
  and and_11 (and_11_out, not_10_out, not_11_out);
  LED TEST_MODE (.in(and_11_out));
  LED RCS_ISP_SCLK (.in(RCS_ISP_OUT_out[0]));
  LED RCS_ISP_MOSI (.in(RCS_ISP_OUT_out[1]));
  LED RCS_ISP_RST (.in(RCS_ISP_OUT_out[2]));
  Random #(.width(1)) random_3 (.clk(RCS_ISP_OUT_out[0]), .next(1'b1), .out(random_3_out));  // open: clr
  LED DCS_ISP_SCLK (.in(DCS_ISP_OUT_out[0]));
  LED DCS_ISP_MOSI (.in(DCS_ISP_OUT_out[1]));
  LED DCS_ISP_RST (.in(DCS_ISP_OUT_out[2]));
  Random #(.width(1)) random_4 (.clk(DCS_ISP_OUT_out[0]), .next(1'b1), .out(random_4_out));  // open: clr
  LED TCS_ISP_SCLK (.in(TCS_ISP_OUT_out[0]));
  LED TCS_ISP_MOSI (.in(TCS_ISP_OUT_out[1]));
  LED TCS_ISP_RST (.in(TCS_ISP_OUT_out[2]));
  Random #(.width(1)) random_5 (.clk(TCS_ISP_OUT_out[0]), .next(1'b1), .out(random_5_out));  // open: clr
  LED DCS_ISP_MISO (.in(random_3_out));
  LED DCS_ISP_MOSI_2 (.in(random_4_out));
  LED DCS_ISP_MOSI_3 (.in(random_5_out));

  assign BUSCTL0 = BC0;
  assign BUSCTL_1 = BC1;

  // Notes on the sheet:
  //   NOT Gates: CD4069, or 74HC04
  //   & Gates:  CD4081 or 74HCx08
  //   MODE SELECT PUSHBUTTON
  //   modelling only -- represents a real SPI bus signal traffic
  //   CD4516 4-stage up counter
  //   SPI isolators/3-state buffers 74HC125?
endmodule
